# Fritzing sketch gardmon (saved by Fritzing 0.9.3b)
breadboards: 1

parts:
  Part1 = Arduino Uno (Rev3)
  DHT1 = DHT22 Humidity and Temperature Sensor
  ZS-042_RTC1 = ZS-042 RTC Module
  R1 = Resistor [tolerance=±5% resistance=100k package=THT]

nets:
  N1: Part1.A4/SDA, ZS-042_RTC1.SDA
  N2: Part1.A5/SCL, ZS-042_RTC1.SCL
  N3: Part1.D2, DHT1.DATA, R1.Pin_1
  5V: Part1.5V, DHT1.VDD, ZS-042_RTC1.VCC, R1.Pin_0
  GND: Part1.GND, DHT1.GND, ZS-042_RTC1.GND
